# Fritzing sketch CCS 881 Sentsorea (saved by Fritzing 0.9.3b)
breadboards: 1

parts:
  Mod1 = CJMCU-811
  Componente1 = Arduino Nano (Rev3.0) (ICSP)

nets:
  VCC: Mod1.VCC, Componente1.3V3
  GND: Mod1.GND, Componente1.GND
  N1: Mod1.SCL, Componente1.A4
  N2: Mod1.SDA, Componente1.A5

custom parts:
  CJMCU-811: The CCS811 is an ultra-low power digital gas sensor solution which integrates a metal oxide (MOX) gas sensor to detect a wide range of Volatile Organic Compounds (VOCs) for indoor air quality monitoring with a microcontroller unit (MCU), which includes an Analog-to-Digital converter (ADC), and an I²C interface.
