# Fritzing sketch DHT11 + CCS811 + LORA OLED (saved by Fritzing 0.9.3b)
breadboards: 1

parts:
  Heltec_WiFi_LoRa_32_V1 = Heltec WiFi LoRa 32 V2 [part_number=HTIT-WB32LA]
  Mod1 = CJMCU-811
  Componente1 = DHT22 module

nets:
  N1: Heltec_WiFi_LoRa_32_V1.pin_1, Mod1.SCL
  VCC: Heltec_WiFi_LoRa_32_V1.pin_16, Heltec_WiFi_LoRa_32_V1.pin_17, Mod1.VCC, Componente1.VCC
  GND: Heltec_WiFi_LoRa_32_V1.pin_18, Heltec_WiFi_LoRa_32_V1.pin_19, Mod1.GND, Mod1.WAK, Componente1.GND
  N2: Heltec_WiFi_LoRa_32_V1.pin_21, Heltec_WiFi_LoRa_32_V1.pin_22
  N3: Heltec_WiFi_LoRa_32_V1.pin_27, Mod1.SDA
  N4: Heltec_WiFi_LoRa_32_V1.pin_35, Componente1.DATA

custom parts:
  Heltec WiFi LoRa 32 V2: Heltec WiFi LoRa 32 V2 WiFi LoRa 32 is a classic IoT dev-board designed & produced by Heltec Automation(TM). It’s a highly integrated product based on ESP32 + SX127x, it has Wi-Fi, BLE, LoRa functions, also Li-Po battery management system, 0.96″ OLED are also included. It’s the best choice for smart cities, smart farms, smart home, and IoT makers.
  CJMCU-811: The CCS811 is an ultra-low power digital gas sensor solution which integrates a metal oxide (MOX) gas sensor to detect a wide range of Volatile Organic Compounds (VOCs) for indoor air quality monitoring with a microcontroller unit (MCU), which includes an Analog-to-Digital converter (ADC), and an I²C interface.
