# Fritzing sketch DHT11 sentsorea (saved by Fritzing 0.9.3b)
breadboards: 1

parts:
  Componente1 = DHT22 module
  R1 = Resistor [tolerance=±5% resistance=10k package=THT]
  Componente2 = Arduino Nano (Rev3.0)

nets:
  N1: Componente1.VCC, Componente2.D11/MOSI
  N2: Componente1.DATA, R1.Pin_0
  N3: R1.Pin_1, Componente2.D4
