# Fritzing sketch LM2596 + LORA OLED + CCS811 + DHT11 (saved by Fritzing 0.9.3b)
breadboards: 1

parts:
  U1 = LM2596-Step-Down-Converter [package=THT]
  Heltec_WiFi_LoRa_32_V1 = Heltec WiFi LoRa 32 V2 [part_number=HTIT-WB32LA]
  Mod1 = CJMCU-811
  Componente1 = DHT22 module
  Componente2 = 12 NeoPixel Ring [part_number=1643]

nets:
  VCC: U1.pin3, Heltec_WiFi_LoRa_32_V1.pin_16, Heltec_WiFi_LoRa_32_V1.pin_17, Mod1.VCC, Componente1.VCC, Componente2.VDD
  GND: U1.pin4, Heltec_WiFi_LoRa_32_V1.pin_18, Heltec_WiFi_LoRa_32_V1.pin_19, Mod1.GND, Mod1.WAK, Componente1.GND, Componente2.OUT, Componente2.GND
  N1: Heltec_WiFi_LoRa_32_V1.pin_1, Heltec_WiFi_LoRa_32_V1.pin_32, Mod1.SCL
  N2: Heltec_WiFi_LoRa_32_V1.pin_2, Componente2.IN
  N3: Heltec_WiFi_LoRa_32_V1.pin_21, Heltec_WiFi_LoRa_32_V1.pin_22
  N4: Heltec_WiFi_LoRa_32_V1.pin_27, Heltec_WiFi_LoRa_32_V1.pin_34, Mod1.SDA
  N5: Heltec_WiFi_LoRa_32_V1.pin_35, Componente1.DATA

custom parts:
  LM2596-Step-Down-Converter: A dummy, proxy, ersatz, stand-in part for whatever you want. With 4 pins on a 100 mil inline pin header footprint.
  Heltec WiFi LoRa 32 V2: Heltec WiFi LoRa 32 V2 WiFi LoRa 32 is a classic IoT dev-board designed & produced by Heltec Automation(TM). It’s a highly integrated product based on ESP32 + SX127x, it has Wi-Fi, BLE, LoRa functions, also Li-Po battery management system, 0.96″ OLED are also included. It’s the best choice for smart cities, smart farms, smart home, and IoT makers.
  CJMCU-811: The CCS811 is an ultra-low power digital gas sensor solution which integrates a metal oxide (MOX) gas sensor to detect a wide range of Volatile Organic Compounds (VOCs) for indoor air quality monitoring with a microcontroller unit (MCU), which includes an Analog-to-Digital converter (ADC), and an I²C interface.
  12 NeoPixel Ring: 12 ultra bright smart LED NeoPixels are arranged in a circle with 1.5" (37mm) outer diameter. The rings are 'chainable' - connect the output pin of one to the input pin of another. Use only one microcontroller pin to control as many as you can chain together! Each LED is addressable as the driver chip is inside the LED. Each one has ~18mA constant current drive so the color will be very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
