# Fritzing sketch Led Neopixel + Lora Oled (saved by Fritzing 0.9.3b)
breadboards: 1

parts:
  Componente1 = 12 NeoPixel Ring [part_number=1643]
  Heltec_WiFi_LoRa_32_V1 = Heltec WiFi LoRa 32 V2 [part_number=HTIT-WB32LA]
  R1 = Resistor [tolerance=±5% resistance=470 package="2512 [SMD]"]

nets:
  N1: Componente1.IN, R1.Pin_1
  N2: Componente1.OUT, Componente1.GND, Heltec_WiFi_LoRa_32_V1.pin_18, Heltec_WiFi_LoRa_32_V1.pin_19
  N3: Componente1.VDD, Heltec_WiFi_LoRa_32_V1.pin_16, Heltec_WiFi_LoRa_32_V1.pin_17
  N4: Heltec_WiFi_LoRa_32_V1.pin_2, R1.Pin_0
  N5: Heltec_WiFi_LoRa_32_V1.pin_21, Heltec_WiFi_LoRa_32_V1.pin_22

custom parts:
  12 NeoPixel Ring: 12 ultra bright smart LED NeoPixels are arranged in a circle with 1.5" (37mm) outer diameter. The rings are 'chainable' - connect the output pin of one to the input pin of another. Use only one microcontroller pin to control as many as you can chain together! Each LED is addressable as the driver chip is inside the LED. Each one has ~18mA constant current drive so the color will be very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
  Heltec WiFi LoRa 32 V2: Heltec WiFi LoRa 32 V2 WiFi LoRa 32 is a classic IoT dev-board designed & produced by Heltec Automation(TM). It’s a highly integrated product based on ESP32 + SX127x, it has Wi-Fi, BLE, LoRa functions, also Li-Po battery management system, 0.96″ OLED are also included. It’s the best choice for smart cities, smart farms, smart home, and IoT makers.
