# Fritzing sketch EskemaOsoaErronka (saved by Fritzing 0.9.3b)
breadboards: 1

parts:
  Componente1 = NeoPixel Stick [part_number=1426]
  DHT2 = DHT11 Humitidy and Temperature Sensor (3 pins)
  Mod2 = CJMCU-811
  Heltec_WiFi_LoRa_2 = Heltec WiFi LoRa 32 [part_number=HTIT-WB32LA]
  HLK-PM2 = HLK-PM01
  R2 = Resistor [tolerance=±5% resistance=470 package="0805 [SMD]"]

nets (from the schematic view):
  GND: Componente1.GND, DHT2.GND
  N1: Componente1.DATAIN, R2.Pin_1
  N2: DHT2.DATA, Heltec_WiFi_LoRa_2.pin_35
  VDD: DHT2.VDD, Mod2.VCC
  N3: Mod2.GND, Mod2.WAK
  N4: Mod2.SCL, Heltec_WiFi_LoRa_2.pin_34
  N5: Mod2.SDA, Heltec_WiFi_LoRa_2.pin_31
  N6: Heltec_WiFi_LoRa_2.pin_2, R2.Pin_0
  N7: Heltec_WiFi_LoRa_2.pin_16, Heltec_WiFi_LoRa_2.pin_21, HLK-PM2.+Vo
  N8: Heltec_WiFi_LoRa_2.pin_17, Heltec_WiFi_LoRa_2.pin_20
  N9: Heltec_WiFi_LoRa_2.pin_18, Heltec_WiFi_LoRa_2.pin_19, Heltec_WiFi_LoRa_2.pin_22, HLK-PM2.-Vo

custom parts:
  NeoPixel Stick: Make your own little LED strip arrangement with this stick of NeoPixel LEDs. We crammed 8 of the tiny 5050 (5mm x 5mm) smart RGB LEDs onto a PCB with mounting holes and a chainable design. Use only one microcontroller pin to control as many as you can chain together! Each LED is addressable as the driver chip is inside the LED. Each one has ~18mA constant current drive so the color will be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
  DHT11 Humitidy and Temperature Sensor (3 pins): DHT11 Humidity and Temperature Sensor (3 pins) from the design created by John De Cristofaro for Adafruit Industries.
  CJMCU-811: The CCS811 is an ultra-low power digital gas sensor solution which integrates a metal oxide (MOX) gas sensor to detect a wide range of Volatile Organic Compounds (VOCs) for indoor air quality monitoring with a microcontroller unit (MCU), which includes an Analog-to-Digital converter (ADC), and an I²C interface.
  Heltec WiFi LoRa 32: Heltec WiFi LoRa 32 WiFi LoRa 32 is a classic IoT dev-board designed & produced by Heltec Automation(TM). It’s a highly integrated product based on ESP32 + SX127x, it has Wi-Fi, BLE, LoRa functions, also Li-Po battery management system, 0.96″ OLED are also included. It’s the best choice for smart cities, smart farms, smart home, and IoT makers.
