# Fritzing sketch DHT11 sentsorea lorarekin (saved by Fritzing 0.9.3b)
breadboards: 1

parts:
  DHT1 = DHT11 Humitidy and Temperature Sensor
  Heltec_WiFi_LoRa_32_V1 = Heltec WiFi LoRa 32 V2 [part_number=HTIT-WB32LA]
  R1 = Resistor [tolerance=±5% resistance=220 package=THT]

nets:
  N1: DHT1.VDD, Heltec_WiFi_LoRa_32_V1.pin_16, Heltec_WiFi_LoRa_32_V1.pin_17, R1.Pin_1
  N2: DHT1.DATA, Heltec_WiFi_LoRa_32_V1.pin_3, R1.Pin_0
  N3: DHT1.GND, Heltec_WiFi_LoRa_32_V1.pin_18, Heltec_WiFi_LoRa_32_V1.pin_19
  N4: Heltec_WiFi_LoRa_32_V1.pin_21, Heltec_WiFi_LoRa_32_V1.pin_22

custom parts:
  DHT11 Humitidy and Temperature Sensor: DHT11 Humidity and Temperature Sensor
  Heltec WiFi LoRa 32 V2: Heltec WiFi LoRa 32 V2 WiFi LoRa 32 is a classic IoT dev-board designed & produced by Heltec Automation(TM). It’s a highly integrated product based on ESP32 + SX127x, it has Wi-Fi, BLE, LoRa functions, also Li-Po battery management system, 0.96″ OLED are also included. It’s the best choice for smart cities, smart farms, smart home, and IoT makers.
