# Fritzing sketch Untitled Sketch (saved by Fritzing 0.9.3b)
breadboards: 1

parts:
  DHT1 = DHT11 Humitidy and Temperature Sensor (3 pins)
  Componente1 = Arduino Nano (Rev3.0)

nets:
  N1: DHT1.DATA, Componente1.D4
  VDD: DHT1.VDD, Componente1.3V3
  GND: DHT1.GND, Componente1.GND

custom parts:
  DHT11 Humitidy and Temperature Sensor (3 pins): DHT11 Humidity and Temperature Sensor (3 pins) from the design created by John De Cristofaro for Adafruit Industries.
