# Fritzing sketch eskema osoa (saved by Fritzing 0.9.3b)
breadboards: 1

parts:
  DHT1 = DHT11 Humitidy and Temperature Sensor (3 pins)
  Mod1 = CJMCU-811
  Heltec_WiFi_LoRa_1 = Heltec WiFi LoRa 32 [part_number=HTIT-WB32LA]
  HLK-PM1 = HLK-PM01
  R1 = Resistor [tolerance=±5% resistance=470 package="0805 [SMD]"]  # not connected

nets (from the breadboard view):
  N1: DHT1.DATA, Heltec_WiFi_LoRa_1.pin_35
  VDD: DHT1.VDD, Mod1.VCC, Heltec_WiFi_LoRa_1.pin_16, Heltec_WiFi_LoRa_1.pin_21, HLK-PM1.+Vo
  GND: DHT1.GND, Mod1.GND, Mod1.WAK, Heltec_WiFi_LoRa_1.pin_18, Heltec_WiFi_LoRa_1.pin_19, Heltec_WiFi_LoRa_1.pin_22, HLK-PM1.-Vo
  N2: Mod1.SCL, Heltec_WiFi_LoRa_1.pin_34
  N3: Mod1.SDA, Heltec_WiFi_LoRa_1.pin_31
  N4: Heltec_WiFi_LoRa_1.pin_17, Heltec_WiFi_LoRa_1.pin_20

custom parts:
  DHT11 Humitidy and Temperature Sensor (3 pins): DHT11 Humidity and Temperature Sensor (3 pins) from the design created by John De Cristofaro for Adafruit Industries.
  CJMCU-811: The CCS811 is an ultra-low power digital gas sensor solution which integrates a metal oxide (MOX) gas sensor to detect a wide range of Volatile Organic Compounds (VOCs) for indoor air quality monitoring with a microcontroller unit (MCU), which includes an Analog-to-Digital converter (ADC), and an I²C interface.
  Heltec WiFi LoRa 32: Heltec WiFi LoRa 32 WiFi LoRa 32 is a classic IoT dev-board designed & produced by Heltec Automation(TM). It’s a highly integrated product based on ESP32 + SX127x, it has Wi-Fi, BLE, LoRa functions, also Li-Po battery management system, 0.96″ OLED are also included. It’s the best choice for smart cities, smart farms, smart home, and IoT makers.
