# Fritzing sketch NeoPixel (saved by Fritzing 0.9.3b)
breadboards: 1

parts:
  Componente2 = NeoPixel Stick [part_number=1426]
  R3 = Resistor [tolerance=±5% resistance=470 package="0805 [SMD]"]
  Heltec_WiFi_LoRa_3 = Heltec WiFi LoRa 32 [part_number=HTIT-WB32LA]

nets:
  N1: Componente2.GND, Heltec_WiFi_LoRa_3.pin_18, Heltec_WiFi_LoRa_3.pin_19, Heltec_WiFi_LoRa_3.pin_22
  N2: Componente2.+5V, Heltec_WiFi_LoRa_3.pin_16, Heltec_WiFi_LoRa_3.pin_21
  N3: Componente2.DATAIN, R3.Pin_1
  N4: R3.Pin_0, Heltec_WiFi_LoRa_3.pin_2
  N5: Heltec_WiFi_LoRa_3.pin_17, Heltec_WiFi_LoRa_3.pin_20

custom parts:
  NeoPixel Stick: Make your own little LED strip arrangement with this stick of NeoPixel LEDs. We crammed 8 of the tiny 5050 (5mm x 5mm) smart RGB LEDs onto a PCB with mounting holes and a chainable design. Use only one microcontroller pin to control as many as you can chain together! Each LED is addressable as the driver chip is inside the LED. Each one has ~18mA constant current drive so the color will be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
  Heltec WiFi LoRa 32: Heltec WiFi LoRa 32 WiFi LoRa 32 is a classic IoT dev-board designed & produced by Heltec Automation(TM). It’s a highly integrated product based on ESP32 + SX127x, it has Wi-Fi, BLE, LoRa functions, also Li-Po battery management system, 0.96″ OLED are also included. It’s the best choice for smart cities, smart farms, smart home, and IoT makers.
