# Fritzing sketch elikatze iturria (saved by Fritzing 0.9.3b)
breadboards: 1

parts:
  HLK-PM3 = HLK-PM01
  Heltec_WiFi_LoRa_3 = Heltec WiFi LoRa 32 [part_number=HTIT-WB32LA]

nets:
  N1: HLK-PM3.-Vo, HLK-PM3.+Vo, Heltec_WiFi_LoRa_3.pin_18, Heltec_WiFi_LoRa_3.pin_19, Heltec_WiFi_LoRa_3.pin_22
  N2: Heltec_WiFi_LoRa_3.pin_16, Heltec_WiFi_LoRa_3.pin_21
  N3: Heltec_WiFi_LoRa_3.pin_17, Heltec_WiFi_LoRa_3.pin_20

custom parts:
  Heltec WiFi LoRa 32: Heltec WiFi LoRa 32 WiFi LoRa 32 is a classic IoT dev-board designed & produced by Heltec Automation(TM). It’s a highly integrated product based on ESP32 + SX127x, it has Wi-Fi, BLE, LoRa functions, also Li-Po battery management system, 0.96″ OLED are also included. It’s the best choice for smart cities, smart farms, smart home, and IoT makers.
