# Fritzing sketch CCS811.fzzJONS ETA ANDER B (saved by Fritzing 0.9.3b)
breadboards: 1

parts:
  Mod1 = CJMCU-811
  Heltec_WiFi_LoRa_1 = Heltec WiFi LoRa 32 [part_number=HTIT-WB32LA]

nets:
  N1: Mod1.VCC, Heltec_WiFi_LoRa_1.pin_16, Heltec_WiFi_LoRa_1.pin_21
  N2: Mod1.GND, Mod1.WAK, Heltec_WiFi_LoRa_1.pin_18, Heltec_WiFi_LoRa_1.pin_19, Heltec_WiFi_LoRa_1.pin_22
  N3: Mod1.SCL, Heltec_WiFi_LoRa_1.pin_27
  N4: Mod1.SDA, Heltec_WiFi_LoRa_1.pin_1
  N5: Heltec_WiFi_LoRa_1.pin_17, Heltec_WiFi_LoRa_1.pin_20

custom parts:
  CJMCU-811: The CCS811 is an ultra-low power digital gas sensor solution which integrates a metal oxide (MOX) gas sensor to detect a wide range of Volatile Organic Compounds (VOCs) for indoor air quality monitoring with a microcontroller unit (MCU), which includes an Analog-to-Digital converter (ADC), and an I²C interface.
  Heltec WiFi LoRa 32: Heltec WiFi LoRa 32 WiFi LoRa 32 is a classic IoT dev-board designed & produced by Heltec Automation(TM). It’s a highly integrated product based on ESP32 + SX127x, it has Wi-Fi, BLE, LoRa functions, also Li-Po battery management system, 0.96″ OLED are also included. It’s the best choice for smart cities, smart farms, smart home, and IoT makers.
