# Fritzing sketch DHT.JONS_ANDERB (saved by Fritzing 0.9.3b)
breadboards: 1

parts:
  DHT1 = DHT11 Humitidy and Temperature Sensor (3 pins)
  Heltec_WiFi_LoRa_1 = Heltec WiFi LoRa 32 [part_number=HTIT-WB32LA]

nets:
  N1: DHT1.DATA, Heltec_WiFi_LoRa_1.pin_35
  N2: DHT1.VDD, Heltec_WiFi_LoRa_1.pin_16, Heltec_WiFi_LoRa_1.pin_21
  N3: DHT1.GND, Heltec_WiFi_LoRa_1.pin_18, Heltec_WiFi_LoRa_1.pin_19, Heltec_WiFi_LoRa_1.pin_22
  N4: Heltec_WiFi_LoRa_1.pin_17, Heltec_WiFi_LoRa_1.pin_20

custom parts:
  DHT11 Humitidy and Temperature Sensor (3 pins): DHT11 Humidity and Temperature Sensor (3 pins) from the design created by John De Cristofaro for Adafruit Industries.
  Heltec WiFi LoRa 32: Heltec WiFi LoRa 32 WiFi LoRa 32 is a classic IoT dev-board designed & produced by Heltec Automation(TM). It’s a highly integrated product based on ESP32 + SX127x, it has Wi-Fi, BLE, LoRa functions, also Li-Po battery management system, 0.96″ OLED are also included. It’s the best choice for smart cities, smart farms, smart home, and IoT makers.
