# Fritzing sketch eskema osoa JONS ETA ANDERB (saved by Fritzing 0.9.3b)
breadboards: 2

parts:
  U1 = LM2596-Step-Down-Converter [package=THT]
  DHT1 = DHT11 Humitidy and Temperature Sensor (3 pins)
  Mod1 = CJMCU-811
  Heltec_WiFi_LoRa_1 = Heltec WiFi LoRa 32 [part_number=HTIT-WB32LA]
  Part3 = 12 NeoPixel Ring [part_number=1643]

nets:
  VDD: U1.pin3, DHT1.VDD, Mod1.VCC, Part3.VDD
  GND: U1.pin4, DHT1.GND, Mod1.GND, Mod1.WAK
  N1: DHT1.DATA, Heltec_WiFi_LoRa_1.pin_35
  N2: Mod1.SCL, Heltec_WiFi_LoRa_1.pin_27
  N3: Mod1.SDA, Heltec_WiFi_LoRa_1.pin_1
  N4: Heltec_WiFi_LoRa_1.pin_16, Heltec_WiFi_LoRa_1.pin_21
  N5: Heltec_WiFi_LoRa_1.pin_17, Heltec_WiFi_LoRa_1.pin_20
  N6: Heltec_WiFi_LoRa_1.pin_18, Heltec_WiFi_LoRa_1.pin_19, Heltec_WiFi_LoRa_1.pin_22

custom parts:
  LM2596-Step-Down-Converter: A dummy, proxy, ersatz, stand-in part for whatever you want. With 4 pins on a 100 mil inline pin header footprint.
  DHT11 Humitidy and Temperature Sensor (3 pins): DHT11 Humidity and Temperature Sensor (3 pins) from the design created by John De Cristofaro for Adafruit Industries.
  CJMCU-811: The CCS811 is an ultra-low power digital gas sensor solution which integrates a metal oxide (MOX) gas sensor to detect a wide range of Volatile Organic Compounds (VOCs) for indoor air quality monitoring with a microcontroller unit (MCU), which includes an Analog-to-Digital converter (ADC), and an I²C interface.
  Heltec WiFi LoRa 32: Heltec WiFi LoRa 32 WiFi LoRa 32 is a classic IoT dev-board designed & produced by Heltec Automation(TM). It’s a highly integrated product based on ESP32 + SX127x, it has Wi-Fi, BLE, LoRa functions, also Li-Po battery management system, 0.96″ OLED are also included. It’s the best choice for smart cities, smart farms, smart home, and IoT makers.
  12 NeoPixel Ring: 12 ultra bright smart LED NeoPixels are arranged in a circle with 1.5" (37mm) outer diameter. The rings are 'chainable' - connect the output pin of one to the input pin of another. Use only one microcontroller pin to control as many as you can chain together! Each LED is addressable as the driver chip is inside the LED. Each one has ~18mA constant current drive so the color will be very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
